# Fritzing sketch sketch (saved by Fritzing 0.9.3b)
breadboards: 1

parts:
  Part1 = Arduino Uno (Rev3)
  LED1 = LED - 5mm [color="Red (633nm)" package="5 mm [THT]"]
  LED2 = LED - 5mm [color="Yellow (595nm)" package="5 mm [THT]"]
  R1 = Resistor [tolerance=±5% resistance=220 package=THT]
  R2 = Resistor [tolerance=±5% resistance=220 package=THT]
  LED3 = LED - 5mm [color="Green (570nm)" package="5 mm [THT]"]
  R3 = Resistor [tolerance=±5% resistance=220 package=THT]  # not connected
  hc-sr1 = hc-sr04

nets:
  N1: Part1.D10_PWM/SS, LED1.anode
  N2: Part1.D11_PWM/MOSI, LED2.anode
  N3: Part1.D12/MISO, LED3.anode
  N4: Part1.D4, hc-sr1.Echo
  N5: Part1.D5_PWM, hc-sr1.Trig
  5V: Part1.5V, hc-sr1.VCC
  GND: Part1.GND, R1.Pin_0, R2.Pin_0, hc-sr1.GND
  N6: LED1.cathode, R1.Pin_1
  N7: LED2.cathode, R2.Pin_1
